// Logisim project Control_Unit.circ as structural Verilog: 5 circuits, main circuit Control Unit
module Control_Unit (
  input  END_CS_IN,
  input  RST,
  input  CLK,
  input  [5:0] Func_Code,
  input  [5:0] OP_Code,
  input  Flag,
  output Write_ID,
  output [3:0] ALU_SEL,
  output A_SEL,
  output [1:0] B_SEL,
  output [2:0] RF_Input,
  output [1:0] RF_SEL,
  output [1:0] BC_SEL,
  output [2:0] FLAG_SEL,
  output WRITE_RF,
  output WRITE_PC,
  output Unsigned,
  output DOut_SEL,
  output [1:0] MA_SEL,
  output CS_EN,
  output TTY_EN,
  output RAM_RW,
  output DIn_SEL,
  output Halt,
  output KBD_EN
);

  wire CS_In_Instruction, demultiplexer_1_out1, demultiplexer_2_out1, IDLE_q, not_1_out, or_1_out,
       WAIT_READ_2_q, WAIT_READ_q;

  D_Flip_Flop IDLE (.clk(CLK), .D(demultiplexer_1_out1), .Q(IDLE_q), .preset(RST));  // open: Qn, en, reset
  Demultiplexer demultiplexer_1 (
    .out0(CS_In_Instruction), .out1(demultiplexer_1_out1), .in(IDLE_q), .sel(RST));  // open: en
  or or_1 (or_1_out, CS_In_Instruction, WAIT_READ_q);
  Demultiplexer demultiplexer_2 (
    .out0(Write_ID), .out1(demultiplexer_2_out1), .in(or_1_out), .sel(not_1_out));  // open: en
  not not_1 (not_1_out, END_CS_IN);
  D_Flip_Flop WAIT_READ (.clk(CLK), .D(demultiplexer_2_out1), .Q(WAIT_READ_q), .reset(RST));  // open: Qn, preset, en
  D_Flip_Flop WAIT_READ_2 (.clk(CLK), .D(Write_ID), .Q(WAIT_READ_2_q), .reset(RST));  // open: Qn, preset, en
  Op_Code_Decoder op_code_decoder_1 (
    .o0(OP_Code[0]), .o1(OP_Code[1]), .o2(OP_Code[2]), .o3(OP_Code[3]), .o4(OP_Code[4]), .o5(OP_Code[5]),
    .ENABLE(WAIT_READ_2_q));  // open: zero, beq, special, addi, bne, andi, blez, ori, bgtz, xori, lw, slti, sw, sltiu, stack, bltz
endmodule

module R_Style_DEC (
  input  EN,
  input  [5:0] Func_Code,
  output [3:0] ALU_SEL,
  output ALU_Unsigned,
  output Write_RF,
  output RF_Input,
  output RF_SEL,
  output BC_SEL
);

  wire alu_sel_dec_1_unsigned;
  wire [3:0] alu_sel_dec_1_as0;

  ALU_Sel_Dec alu_sel_dec_1 (
    .f0(Func_Code[0]), .f1(Func_Code[1]), .f2(Func_Code[2]), .f3(Func_Code[3]), .f4(Func_Code[4]),
    .f5(Func_Code[5]), .AS0(alu_sel_dec_1_as0[0]), .AS1(alu_sel_dec_1_as0[1]), .AS2(alu_sel_dec_1_as0[2]),
    .AS4(alu_sel_dec_1_as0[3]), .\unsigned (alu_sel_dec_1_unsigned));
  assign ALU_SEL = {4{EN}} & alu_sel_dec_1_as0;  // AND_Gate and_1, 4 bits wide
  and and_2 (ALU_Unsigned, alu_sel_dec_1_unsigned, EN);
endmodule

module ALU_Sel_Dec (
  input  f0,
  input  f1,
  input  f2,
  input  f3,
  input  f4,
  input  f5,
  output AS0,
  output AS1,
  output AS2,
  output AS4,
  output \unsigned 
);

  wire \and , div, divu, lt, ltu, mul, mulu, \nor , \or , sub, \xor ;

  and and_1 (sub, ~f0, f1, ~f2, ~f3, ~f4, f5);  // AND_Gate
  and and_2 (mul, ~f0, ~f1, ~f2, f3, f4, ~f5);  // AND_Gate
  and and_3 (mulu, f0, ~f1, ~f2, f3, f4, ~f5);  // AND_Gate
  and and_4 (div, ~f0, f1, ~f2, f3, f4, ~f5);  // AND_Gate
  and and_5 (divu, f0, f1, ~f2, f3, f4, ~f5);  // AND_Gate
  and and_6 (\and , ~f0, ~f1, f2, ~f3, ~f4, f5);  // AND_Gate
  and and_7 (\or , f0, ~f1, f2, ~f3, ~f4, f5);  // AND_Gate
  and and_8 (\nor , f0, f1, f2, ~f3, ~f4, f5);  // AND_Gate
  and and_9 (\xor , ~f0, ~f1, ~f2, f3, ~f4, f5);  // AND_Gate
  and and_10 (lt, ~f0, f1, ~f2, f3, ~f4, f5);  // AND_Gate
  and and_11 (ltu, f0, f1, ~f2, f3, ~f4, f5);  // AND_Gate
  or or_1 (AS0, sub, div, divu, \or , \xor , ltu);
  or or_2 (AS1, mul, mulu, div, divu, \nor , \xor );
  or or_3 (AS2, \and , \or , \nor , \xor );
  or or_4 (AS4, lt, ltu);
  or or_5 (\unsigned , mulu, divu);
endmodule

module Op_Code_Decoder (
  input  o0,
  input  o1,
  input  o2,
  input  o3,
  input  o4,
  input  o5,
  input  ENABLE,
  output zero,
  output beq,
  output stack,
  output addi,
  output bne,
  output special,
  output andi,
  output blez,
  output ori,
  output bgtz,
  output xori,
  output bltz,
  output slti,
  output lw,
  output sltiu,
  output sw
);

  wire and_1_out, and_2_out, and_3_out, and_4_out, and_5_out, and_6_out, and_7_out, and_15_out, and_16_out,
       and_17_out, and_18_out, and_19_out, and_20_out, and_21_out, and_29_out, and_30_out;

  and and_1 (and_1_out, ~o0, ~o1, ~o1, ~o3, ~o4, ~o5);  // AND_Gate
  and and_2 (and_2_out, ~o0, ~o1, ~o1, o3, ~o4, ~o5);  // AND_Gate
  and and_3 (and_3_out, ~o0, ~o1, o1, o3, ~o4, ~o5);  // AND_Gate
  and and_4 (and_4_out, o0, ~o1, o1, o3, ~o4, ~o5);  // AND_Gate
  and and_5 (and_5_out, ~o0, o1, o1, o3, ~o4, ~o5);  // AND_Gate
  and and_6 (and_6_out, ~o0, o1, ~o1, o3, ~o4, ~o5);  // AND_Gate
  and and_7 (and_7_out, o0, o1, ~o1, o3, ~o4, ~o5);  // AND_Gate
  and and_8 (zero, and_1_out, ENABLE);
  and and_9 (addi, and_2_out, ENABLE);
  and and_10 (andi, and_3_out, ENABLE);
  and and_11 (ori, and_4_out, ENABLE);
  and and_12 (xori, and_5_out, ENABLE);
  and and_13 (slti, and_6_out, ENABLE);
  and and_14 (sltiu, and_7_out, ENABLE);
  and and_15 (and_15_out, ~o0, ~o1, o1, ~o3, ~o4, ~o5);  // AND_Gate
  and and_16 (and_16_out, o0, ~o1, o1, ~o3, ~o4, ~o5);  // AND_Gate
  and and_17 (and_17_out, ~o0, o1, o1, ~o3, ~o4, ~o5);  // AND_Gate
  and and_18 (and_18_out, o0, o1, o1, ~o3, ~o4, ~o5);  // AND_Gate
  and and_19 (and_19_out, o0, ~o1, ~o1, ~o3, ~o4, ~o5);  // AND_Gate
  and and_20 (and_20_out, o0, o1, ~o1, ~o3, ~o4, o5);  // AND_Gate
  and and_21 (and_21_out, o0, o1, ~o1, o3, ~o4, o5);  // AND_Gate
  and and_22 (beq, and_15_out, ENABLE);
  and and_23 (bne, and_16_out, ENABLE);
  and and_24 (blez, and_17_out, ENABLE);
  and and_25 (bgtz, and_18_out, ENABLE);
  and and_26 (bltz, and_19_out, ENABLE);
  and and_27 (lw, and_20_out, ENABLE);
  and and_28 (sw, and_21_out, ENABLE);
  and and_29 (and_29_out, ~o0, ~o1, ~o1, o3, o4, o5);  // AND_Gate
  and and_30 (and_30_out, o0, o1, o1, o3, o4, o5);
  and and_31 (stack, and_29_out, ENABLE);
  and and_32 (special, and_30_out, ENABLE);

  assign o2 = o1;

  // Other names for the same wires on the sheet: EN = ENABLE
endmodule

module Func_Code_DEC (
  input  f0,
  input  f1,
  input  f2,
  input  f3,
  input  f4,
  input  f5,
  input  EN,
  output add,
  output \and ,
  output nop_pop,
  output sub,
  output \or ,
  output push_tty,
  output mul,
  output \nor ,
  output halt,
  output mulu,
  output \xor ,
  output rnd,
  output kbd,
  output div,
  output mfhi,
  output mflo,
  output divu,
  output slt,
  output jr,
  output sltu
);

  wire and_1_out, and_2_out, and_3_out, and_4_out, and_5_out, and_6_out, and_7_out, and_8_out, and_17_out,
       and_18_out, and_19_out, and_20_out, and_21_out, and_22_out, and_23_out, and_31_out, and_32_out,
       and_33_out, and_34_out, and_35_out;

  and and_1 (and_1_out, ~f0, ~f1, ~f2, ~f3, ~f4, f5);  // AND_Gate
  and and_2 (and_2_out, ~f0, f1, ~f2, ~f3, ~f4, f5);  // AND_Gate
  and and_3 (and_3_out, ~f0, ~f1, ~f2, f3, f4, ~f5);  // AND_Gate
  and and_4 (and_4_out, f0, ~f1, ~f2, f3, f4, ~f5);  // AND_Gate
  and and_5 (and_5_out, ~f0, f1, ~f2, f3, f4, ~f5);  // AND_Gate
  and and_6 (and_6_out, f0, f1, ~f2, f3, f4, ~f5);  // AND_Gate
  and and_7 (and_7_out, ~f0, f1, ~f2, f3, ~f4, f5);  // AND_Gate
  and and_8 (and_8_out, f0, f1, ~f2, f3, ~f4, f5);  // AND_Gate
  and and_9 (add, and_1_out, EN);
  and and_10 (sub, and_2_out, EN);
  and and_11 (mul, and_3_out, EN);
  and and_12 (mulu, and_4_out, EN);
  and and_13 (div, and_5_out, EN);
  and and_14 (divu, and_6_out, EN);
  and and_15 (slt, and_7_out, EN);
  and and_16 (sltu, and_8_out, EN);
  and and_17 (and_17_out, ~f0, ~f1, f2, ~f3, ~f4, f5);  // AND_Gate
  and and_18 (and_18_out, f0, ~f1, f2, ~f3, ~f4, f5);  // AND_Gate
  and and_19 (and_19_out, f0, f1, f2, ~f3, ~f4, f5);  // AND_Gate
  and and_20 (and_20_out, ~f0, ~f1, ~f2, f3, ~f4, f5);  // AND_Gate
  and and_21 (and_21_out, ~f0, ~f1, ~f2, ~f3, f4, ~f5);  // AND_Gate
  and and_22 (and_22_out, ~f0, f1, ~f2, ~f3, f4, ~f5);  // AND_Gate
  and and_23 (and_23_out, ~f0, ~f1, ~f2, f3, ~f4, ~f5);  // AND_Gate
  and and_24 (\and , and_17_out, EN);
  and and_25 (\or , and_18_out, EN);
  and and_26 (\nor , and_19_out, EN);
  and and_27 (\xor , and_20_out, EN);
  and and_28 (mfhi, and_21_out, EN);
  and and_29 (mflo, and_22_out, EN);
  and and_30 (jr, and_23_out, EN);
  and and_31 (and_31_out, ~f0, ~f1, ~f2, ~f3, ~f4, ~f5);  // AND_Gate
  and and_32 (and_32_out, f0, ~f1, ~f2, ~f3, ~f4, ~f5);  // AND_Gate
  and and_33 (and_33_out, f0, f1, f2, f3, f4, f5);
  and and_34 (and_34_out, ~f0, f1, ~f2, ~f3, ~f4, ~f5);  // AND_Gate
  and and_35 (and_35_out, ~f0, ~f1, f2, ~f3, ~f4, ~f5);  // AND_Gate
  and and_36 (nop_pop, and_31_out, EN);
  and and_37 (push_tty, and_32_out, EN);
  and and_38 (halt, and_33_out, EN);
  and and_39 (rnd, and_34_out, EN);
  and and_40 (kbd, and_35_out, EN);
endmodule
